# Fritzing sketch SmartFan (saved by Fritzing 0.9.3b)
breadboards: 1

parts:
  U1 = ESP32S-HiLetgo [part_number=ESP32S-HiLetgo]
  J1 = Piezo Speaker
  C1 = Electrolytic Capacitor [capacitance=10μF package="0605 [SMD, electrolytic]"]
  M1 = RioRand LM2596
  A1 = DHT22 module
  HLK-PM1 = HLK-PM12 [part_number=HLK-PM12]

nets:
  N1: U1.GND, J1.pin1, C1.-, M1.Pin_4, A1.-
  N2: U1.VIN, C1.+, M1.Pin_3, A1.+
  N3: U1.GPIO22, A1.Out
  N4: U1.GPIO23, J1.pin2
  N5: M1.Pin_1, HLK-PM1.+Vo
  N6: M1.Pin_2, HLK-PM1.-Vo

custom parts:
  ESP32S-HiLetgo: HiLetgo ESP-WROOM-32 ESP32 ESP-32S Development Board 2.4GHz Dual-Mode WiFi + Bluetooth Dual Cores Microcontroller The ESP32 integrated with Antenna switches, RF Balun, power amplifiers, low-noise amplifiers, filters, and management modules, and the entire solution occupies the least area of PCB. 2.4 GHz Wi-Fi plus Bluetooth dual-mode chip, with TSMC Ultra-low power consumption 40nm technology,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
  DHT22 module: DHT22 module. Pins VCC Data GND.
